// Logisim project ex_splitters.circ as structural Verilog: 1 circuit, main circuit main
module main (
  output [3:0] out_1,
  output [5:0] out_2,
  output [1:0] out_3,
  output [1:0] out_4,
  output [1:0] out_5,
  output [1:0] out_6,
  output [15:0] out_7
);

  assign out_7 = {{8{1'b1}}, {8{1'b1}}};  // Bit_Extender bit_extender_1

  assign out_1 = 4'b1001;
  assign out_2 = 6'b111001;
  assign out_3 = 2'b01;
  assign out_4 = 2'b10;
  assign out_5 = 2'b11;
  assign out_6 = 2'b11;
endmodule
