// Logisim project control_logic.circ as structural Verilog: 1 circuit, main circuit control_logic
module control_logic (
  input  [31:0] inst,
  input  BrEq,
  input  BrLt,
  output PCSel,
  output RegWEn,
  output [2:0] ImmSel,
  output BrUn,
  output ASel,
  output BSel,
  output [3:0] ALUSel,
  output MemRW,
  output [1:0] WBSel
);

  wire and_1_out, and_3_out, and_5_out, and_8_out, and_9_out, and_10_out, and_11_out, and_12_out, and_13_out,
       and_15_out, and_16_out, and_17_out, and_18_out, and_19_out, and_20_out, and_21_out, and_22_out,
       MemRWS, multiplexer_2_out, not_1_out, not_2_out, not_3_out, not_4_out, not_5_out, not_6_out,
       not_7_out, not_8_out, not_9_out, not_10_out, not_11_out, not_12_out, not_13_out, not_14_out,
       not_15_out, not_16_out, not_17_out, not_18_out, not_19_out, not_20_out, not_21_out, not_22_out,
       not_23_out, not_24_out, not_25_out, not_26_out, not_27_out, not_28_out, not_29_out, not_30_out,
       not_31_out, not_32_out, not_33_out, not_34_out, not_35_out, not_36_out, not_37_out, not_38_out,
       not_39_out, not_40_out, not_41_out, not_42_out, not_43_out, not_44_out, not_45_out, not_46_out,
       not_47_out, or_5_out, PCSelSB, sel0, sel1, sel2, sel3;
  wire [3:0] ALUI, ALUR, Rtypec;
  wire [3:1] Rtypea;

  not not_1 (not_1_out, inst[25]);
  not not_2 (not_2_out, inst[3]);
  and and_1 (and_1_out, not_1_out, inst[26]);
  or or_1 (Rtypea[3], and_1_out, and_3_out);
  not not_3 (not_3_out, inst[4]);
  and and_2 (sel3, inst[2], not_2_out, not_3_out, inst[5], inst[6]);
  not not_4 (not_4_out, inst[26]);
  and and_3 (and_3_out, inst[25], not_4_out);
  not not_5 (not_5_out, inst[25]);
  and and_4 (Rtypea[2], not_5_out, inst[26]);
  not not_6 (not_6_out, inst[3]);
  not not_7 (not_7_out, inst[2]);
  not not_8 (not_8_out, inst[3]);
  not not_9 (not_9_out, inst[4]);
  and and_5 (and_5_out, inst[5], not_9_out, not_8_out, not_7_out, inst[6]);
  not not_10 (not_10_out, inst[26]);
  and and_6 (Rtypea[1], inst[25], not_10_out);
  not not_11 (not_11_out, inst[30]);
  and and_7 (Rtypec[3], inst[25], not_11_out);
  not not_12 (not_12_out, inst[3]);
  not not_13 (not_13_out, inst[5]);
  not not_14 (not_14_out, inst[6]);
  and and_8 (and_8_out, inst[2], not_12_out, inst[4], not_17_out, inst[5]);
  and and_9 (and_9_out, inst[2], not_6_out, inst[4], not_13_out, not_14_out);
  or or_2 (sel2, and_5_out, and_9_out, and_8_out, and_11_out);
  not not_15 (not_15_out, inst[25]);
  and and_10 (and_10_out, not_15_out, not_19_out);
  not not_16 (not_16_out, inst[4]);
  not not_17 (not_17_out, inst[6]);
  and and_11 (and_11_out, inst[2], inst[3], not_16_out, inst[5], inst[6]);
  not not_18 (not_18_out, inst[25]);
  not not_19 (not_19_out, inst[30]);
  or or_3 (Rtypec[2], and_10_out, and_12_out);
  Multiplexer #(.select(3), .width(4), .enable("false")) multiplexer_1 (
    .in0({Rtypea, 1'b0}), .in1({inst[25], 3'b110}), .in2(4'b0111), .in3(4'b1011), .in4(4'b0011),
    .in5({Rtypec[3:2], 1'b0, Rtypec[0]}), .in6(4'b0010), .in7({inst[25], 3'b001}), .out(ALUR),
    .sel(inst[14:12]));
  and and_12 (and_12_out, not_18_out, inst[30]);
  not not_20 (not_20_out, inst[5]);
  not not_21 (not_21_out, inst[6]);
  not not_22 (not_22_out, inst[3]);
  not not_23 (not_23_out, inst[2]);
  not not_24 (not_24_out, inst[2]);
  and and_13 (and_13_out, not_22_out, not_20_out, not_21_out, not_24_out, inst[4]);
  not not_25 (not_25_out, inst[25]);
  and and_14 (Rtypec[0], not_25_out, inst[30]);
  not not_26 (not_26_out, inst[4]);
  not not_27 (not_27_out, inst[3]);
  not not_28 (not_28_out, inst[6]);
  and and_15 (and_15_out, not_23_out, not_27_out, not_26_out, inst[5], not_28_out);
  or or_4 (sel1, and_13_out, and_15_out, and_17_out, and_16_out);
  not not_29 (not_29_out, inst[4]);
  not not_30 (not_30_out, inst[3]);
  not not_31 (not_31_out, inst[6]);
  and and_16 (and_16_out, inst[2], inst[3], not_29_out, inst[5], inst[6]);
  and and_17 (and_17_out, inst[2], inst[4], not_30_out, not_31_out, inst[5]);
  not not_32 (not_32_out, BrLt);
  not not_33 (not_33_out, BrEq);
  and and_18 (and_18_out, BrEq, not_32_out);
  not not_34 (not_34_out, inst[5]);
  not not_35 (not_35_out, inst[2]);
  not not_36 (not_36_out, inst[4]);
  not not_37 (not_37_out, inst[3]);
  and and_19 (and_19_out, not_35_out, not_37_out, not_36_out, not_34_out, not_41_out);
  not not_38 (not_38_out, BrLt);
  or or_5 (or_5_out, BrEq, not_38_out);
  not not_39 (not_39_out, inst[3]);
  not not_40 (not_40_out, inst[2]);
  not not_41 (not_41_out, inst[6]);
  not not_42 (not_42_out, inst[4]);
  and and_20 (and_20_out, not_40_out, not_39_out, not_42_out, inst[5], not_43_out);
  not not_43 (not_43_out, inst[6]);
  not not_44 (not_44_out, inst[3]);
  or or_6 (sel0, and_19_out, and_20_out, and_21_out, and_22_out);
  Multiplexer #(.enable("false")) multiplexer_2 (.in0(1'b0), .in1(1'b1), .out(multiplexer_2_out), .sel(BrLt));
  Multiplexer #(.select(3), .enable("false")) multiplexer_3 (
    .in0(and_18_out), .in1(not_33_out), .in4(BrLt), .in5(or_5_out), .in6(BrLt), .in7(or_5_out),
    .out(PCSelSB), .sel(inst[14:12]));  // open: in2, in3
  not not_45 (not_45_out, inst[5]);
  not not_46 (not_46_out, inst[6]);
  and and_21 (and_21_out, inst[2], not_44_out, inst[4], not_45_out, not_46_out);
  Multiplexer #(.select(3), .enable("false")) multiplexer_4 (
    .in0(1'b0), .in1(1'b0), .in4(1'b0), .in5(1'b0), .in6(1'b1), .in7(1'b1), .out(BrUn), .sel(inst[14:12]));  // open: in2, in3
  Multiplexer #(.select(4), .width(4), .enable("false")) multiplexer_5 (
    .in0(ALUR), .in1(4'b0000), .in2(ALUI), .in3(ALUI), .in4(ALUI), .in5(4'b0000), .in6(4'b1101),
    .in7(4'b0000), .in8(4'b0000), .out(ALUSel), .sel({sel3, sel2, sel1, sel0}));  // open: in9, in10, in11, in12, in13, in14, in15
  not not_47 (not_47_out, inst[4]);
  and and_22 (and_22_out, inst[2], inst[3], not_47_out, inst[5], inst[6]);
  Multiplexer #(.select(3), .enable("false")) multiplexer_6 (
    .in2(1'b1), .in7(multiplexer_2_out), .out(MemRWS), .sel(inst[14:12]));  // open: in0, in1, in3, in4, in5, in6
  Multiplexer #(.select(4), .enable("false")) multiplexer_7 (
    .in0(1'b1), .in1(1'b1), .in2(1'b1), .in3(1'b0), .in4(1'b0), .in5(1'b1), .in6(1'b1), .in7(1'b1),
    .in8(1'b1), .out(RegWEn), .sel({sel3, sel2, sel1, sel0}));  // open: in9, in10, in11, in12, in13, in14, in15
  Multiplexer #(.select(3), .width(4), .enable("false")) multiplexer_8 (
    .in0(4'b0000), .in1(4'b0110), .in2(4'b0111), .in3(4'b0011), .in4(4'b0100), .in5({3'b010, inst[30]}),
    .in6(4'b0010), .in7(4'b0001), .out(ALUI), .sel(inst[14:12]));
  Multiplexer #(.select(4), .width(3), .enable("false")) multiplexer_9 (
    .in1(3'b000), .in2(3'b000), .in3(3'b001), .in4(3'b010), .in5(3'b011), .in6(3'b011), .in7(3'b010),
    .in8(3'b000), .out(ImmSel), .sel({sel3, sel2, sel1, sel0}));  // open: in0, in9, in10, in11, in12, in13, in14, in15
  Multiplexer #(.select(4), .width(2), .enable("false")) multiplexer_10 (
    .in0(2'b01), .in1(2'b11), .in2(2'b10), .in3(2'b10), .in4(2'b10), .in5(2'b01), .in6(2'b01), .in7(2'b00),
    .in8(2'b00), .out(WBSel), .sel({sel3, sel2, sel1, sel0}));  // open: in9, in10, in11, in12, in13, in14, in15
  Multiplexer #(.select(4), .enable("false")) multiplexer_11 (
    .in0(1'b0), .in1(1'b0), .in2(1'b0), .in3(1'b0), .in4(PCSelSB), .in5(1'b0), .in6(1'b0), .in7(1'b1),
    .in8(1'b1), .out(PCSel), .sel({sel3, sel2, sel1, sel0}));  // open: in9, in10, in11, in12, in13, in14, in15
  Multiplexer #(.select(4), .enable("false")) multiplexer_12 (
    .in0(1'b0), .in1(1'b0), .in2(1'b0), .in3(MemRWS), .in4(1'b0), .in5(1'b0), .in6(1'b0), .in7(1'b0),
    .in8(1'b0), .in9(1'b0), .out(MemRW), .sel({sel3, sel2, sel1, sel0}));  // open: in10, in11, in12, in13, in14, in15
  Multiplexer #(.select(4), .enable("false")) multiplexer_13 (
    .in0(1'b0), .in1(1'b0), .in2(1'b0), .in3(1'b0), .in4(1'b1), .in5(1'b1), .in6(1'b1), .in7(1'b1),
    .in8(1'b0), .out(ASel), .sel({sel3, sel2, sel1, sel0}));  // open: in9, in10, in11, in12, in13, in14, in15
  Multiplexer #(.select(4), .enable("false")) multiplexer_14 (
    .in0(1'b0), .in1(1'b1), .in2(1'b1), .in3(1'b1), .in4(1'b1), .in5(1'b1), .in6(1'b1), .in7(1'b1),
    .in8(1'b1), .out(BSel), .sel({sel3, sel2, sel1, sel0}));  // open: in9, in10, in11, in12, in13, in14, in15

  // Other names for the same wires on the sheet: fa5 = inst[30]; func7[6:0] = inst[31:25]; opcode[6:0] = inst[6:0];
  //   op2 = inst[2]; op3 = inst[3]; op4 = inst[4]; op5 = inst[5]; op6 = inst[6]; func3[2:0] = inst[14:12];
  //   fa1 = inst[26]; fa0 = inst[25]; Rtypeb[3] = inst[25]; Rtyped[3] = inst[25];
  //   typesel[3:0] = {sel3, sel2, sel1, sel0}

  // Notes on the sheet:
  //   INPUTS to your circuit
  //   DON'T CHANGE THE LOCATIONS OF THE INPUTS AND OUTPUTS!
  //   OUTPUT from your circuit
  //   RType
  //   TypeSelector
  //   SType
  //   SBType
  //   UJType
  //   UJType
  //   IType
  //   ITypeUp
  //   UTypeu
  //   UTyped
  //   RegWEn
  //   MemRWSel
  //   WBSel
  //   immSel
  //   ASel
  //   BSel
  //   PCSel
endmodule
