// Logisim project cpu.circ as structural Verilog: 1 circuit, main circuit main
// widthSel
module main (
  input  [31:0] INSTRUCTION,
  input  CLOCK,
  output [31:0] PROGRAM_COUNTER,
  output [31:0] ra,
  output [31:0] sp,
  output [31:0] t0,
  output [31:0] t1,
  output [31:0] t2,
  output [31:0] s0,
  output [31:0] s1,
  output [31:0] a0
);

  wire ASel, branch_comp_1_breq, branch_comp_1_brlt, BSel, control_logic_1_brun, control_logic_1_memrw,
       PCSel, register_2_q, RWen;
  wire [1:0] control_logic_1_wbsel;
  wire [2:0] control_logic_1_immsel, widthSel;
  wire [3:0] ALUSel;
  wire [4:0] multiplexer_2_out_2, multiplexer_2_out_3;
  wire [6:0] multiplexer_2_out_4;
  wire [7:0] bit_extender_1_out;
  wire [11:0] multiplexer_2_out;
  wire [15:0] bit_extender_4_out;
  wire [31:0] adder_1_out, adder_2_out, ALUr, bit_extender_2_out, bit_extender_3_out, DMEM_p5, ID_q, imm,
       multiplexer_1_out, multiplexer_3_out, multiplexer_4_out, multiplexer_5_out, RegFile_read_data_2,
       register_1_q, rs1d, WB;

  Adder #(.width(32)) adder_1 (.a(PROGRAM_COUNTER), .b(32'h4), .out(adder_1_out));  // open: cin, cout
  Multiplexer #(.width(32), .enable("false")) multiplexer_1 (
    .in0(adder_1_out), .in1(ALUr), .out(multiplexer_1_out), .sel(PCSel));
  Register #(.width(32)) PC (.D(multiplexer_1_out), .en(1'b1), .clk(CLOCK), .Q(PROGRAM_COUNTER));  // open: clr
  Register #(.width(32)) register_1 (.D(PROGRAM_COUNTER), .en(1'b1), .clk(CLOCK), .Q(register_1_q));  // open: clr
  Register #(.width(32)) ID (.D(INSTRUCTION), .en(1'b1), .clk(CLOCK), .Q(ID_q));  // open: clr
  Register #(.width(1)) register_2 (.D(PCSel), .en(1'b1), .clk(CLOCK), .Q(register_2_q));  // open: clr
  control_logic control_logic_1 (
    .BSel(BSel), .ASel(ASel), .BrUn(control_logic_1_brun), .ImmSel(control_logic_1_immsel), .RegWEn(RWen),
    .PCSel(PCSel), .BrLt(branch_comp_1_brlt), .BrEq(branch_comp_1_breq),
    .inst({multiplexer_2_out_4, multiplexer_2_out_3, multiplexer_2_out_2, widthSel, multiplexer_2_out}),
    .ALUSel(ALUSel), .MemRW(control_logic_1_memrw), .WBSel(control_logic_1_wbsel));
  Multiplexer #(.width(32), .enable("false")) multiplexer_2 (
    .in0(ID_q), .in1(32'h13),
    .out({multiplexer_2_out_4, multiplexer_2_out_3, multiplexer_2_out_2, widthSel, multiplexer_2_out}),
    .sel(register_2_q));
  regfile_main RegFile (
    .rs2(multiplexer_2_out_2), .rd(multiplexer_2_out[11:7]), .Read_Data_1(rs1d),
    .Read_Data_2(RegFile_read_data_2), .ra(ra), .sp(sp), .t0(t0), .t1(t1), .t2(t2), .s0(s0), .s1(s1),
    .a0(a0), .rs1(multiplexer_2_out_3), .Write_Data(WB), .RegWEn(RWen), .clk(CLOCK));
  imm_gen imm_gen_1 (
    .ImmSel(control_logic_1_immsel), .imm(imm),
    .inst({multiplexer_2_out_4, multiplexer_2_out_3, multiplexer_2_out_2, widthSel, multiplexer_2_out}));
  Multiplexer #(.width(32), .enable("false")) multiplexer_3 (
    .in0(rs1d), .in1(register_1_q), .out(multiplexer_3_out), .sel(ASel));
  Multiplexer #(.width(32), .enable("false")) multiplexer_4 (
    .in0(RegFile_read_data_2), .in1(imm), .out(multiplexer_4_out), .sel(BSel));
  branch_comp branch_comp_1 (
    .BrEq(branch_comp_1_breq), .BrUn(control_logic_1_brun), .rs1(multiplexer_3_out),
    .BrLt(branch_comp_1_brlt), .rs2(multiplexer_4_out));
  alu Arithmetic_Logic_Unit (.ALUSel(ALUSel), .Result(ALUr), .A(multiplexer_3_out), .B(multiplexer_4_out));
  // mem_main DMEM: pin names not known; wires that end beside it: ALUr, rs1d, CLOCK, control_logic_1_memrw, DMEM_p5
  Bit_Extender #(.in_width(32), .out_width(8)) bit_extender_1 (.in(DMEM_p5), .out(bit_extender_1_out));
  assign bit_extender_2_out = {{24{bit_extender_1_out[7]}}, bit_extender_1_out};  // Bit_Extender bit_extender_2
  assign bit_extender_3_out = {{16{bit_extender_4_out[15]}}, bit_extender_4_out};  // Bit_Extender bit_extender_3
  Bit_Extender #(.in_width(32)) bit_extender_4 (.in(DMEM_p5), .out(bit_extender_4_out));
  Adder #(.width(32)) adder_2 (.a(register_1_q), .b(32'h4), .out(adder_2_out));  // open: cin, cout
  Multiplexer #(.select(3), .width(32), .enable("false")) multiplexer_5 (
    .in0(bit_extender_2_out), .in1(bit_extender_3_out), .in2(DMEM_p5), .out(multiplexer_5_out), .sel(widthSel));  // open: in3, in4, in5, in6, in7
  Multiplexer #(.select(2), .width(32), .enable("false")) multiplexer_6 (
    .in0(adder_2_out), .in1(ALUr), .in2(DMEM_p5), .in3(multiplexer_5_out), .out(WB),
    .sel(control_logic_1_wbsel));

  // Other names for the same wires on the sheet: clk = CLOCK

  // Notes on the sheet:
  //   Output
  //   IMEM (do **NOT** move this)
  //   Inputs
  //   Inputs/Outputs for testing. Do **NOT** move these.
endmodule
