// Logisim project alu.circ as structural Verilog: 1 circuit, main circuit alu
module alu (
  input  [31:0] A,
  input  [31:0] B,
  input  [3:0] ALUSel,
  output [31:0] Result
);

  wire bitselector_1_out, bitselector_2_out, comparator_1_lt;
  wire [4:0] bit_extender_1_out, bit_extender_2_out, bit_extender_5_out;
  wire [31:0] add0, adder_2_out, and0, bit_extender_3_out, bit_extender_4_out, divu, mul0, mulh, mulhu,
       multiplier_2_out, multiplier_3_out, or0, remu, sll0, slt0, sra0, srl0, sub0, xor0;

  Adder #(.width(32)) adder_1 (.a(A), .b(B), .out(add0));  // open: cin, cout
  assign and0 = A & B;  // AND_Gate and_1, 32 bits wide
  assign or0 = A | B;  // OR_Gate or_1, 32 bits wide
  assign xor0 = A ^ B;  // XOR_Gate xor_1, 32 bits wide
  Shifter #(.width(32), .shift("lr")) shifter_1 (.in(A), .\dist (bit_extender_1_out), .out(srl0));
  Bit_Extender #(.in_width(32), .out_width(5)) bit_extender_1 (.in(B), .out(bit_extender_1_out));
  Shifter #(.width(32), .shift("ar")) shifter_2 (.in(A), .\dist (bit_extender_2_out), .out(sra0));
  Bit_Extender #(.in_width(32), .out_width(5)) bit_extender_2 (.in(B), .out(bit_extender_2_out));
  Multiplier #(.width(32)) multiplier_1 (.a(A), .b(B), .out(mul0), .cout(mulhu));  // open: cin
  BitSelector #(.width(32)) bitselector_1 (.in(A), .out(bitselector_1_out), .sel({5{1'b1}}));
  BitSelector #(.width(32)) bitselector_2 (.in(B), .out(bitselector_2_out), .sel({5{1'b1}}));
  assign bit_extender_3_out = {{31{bitselector_1_out}}, bitselector_1_out};  // Bit_Extender bit_extender_3
  assign bit_extender_4_out = {{31{bitselector_2_out}}, bitselector_2_out};  // Bit_Extender bit_extender_4
  Multiplier #(.width(32)) multiplier_2 (.a(B), .b(bit_extender_3_out), .out(multiplier_2_out));  // open: cin, cout
  Multiplier #(.width(32)) multiplier_3 (.a(bit_extender_4_out), .b(A), .out(multiplier_3_out));  // open: cin, cout
  Adder #(.width(32)) adder_2 (.a(mulhu), .b(multiplier_2_out), .out(adder_2_out));  // open: cin, cout
  Divider #(.width(32)) divider_1 (.a(A), .b(B), .out(divu), .rem(remu));  // open: upper
  Subtractor #(.width(32)) subtractor_1 (.a(A), .b(B), .out(sub0));  // open: bin, bout
  Adder #(.width(32)) adder_3 (.a(adder_2_out), .b(multiplier_3_out), .out(mulh));  // open: cin, cout
  Bit_Extender #(.in_width(32), .out_width(5)) bit_extender_5 (.in(B), .out(bit_extender_5_out));
  Multiplexer #(.select(4), .width(32), .enable("false")) multiplexer_1 (
    .in0(add0), .in1(and0), .in2(or0), .in3(xor0), .in4(srl0), .in5(sra0), .in6(sll0), .in7(slt0),
    .in8(divu), .in9(remu), .in10(mul0), .in11(mulhu), .in12(sub0), .in13(B), .in14(mulh), .out(Result),
    .sel(ALUSel));  // open: in15
  Shifter #(.width(32)) shifter_3 (.in(A), .\dist (bit_extender_5_out), .out(sll0));
  Comparator #(.width(32)) comparator_1 (.a(A), .b(B), .lt(comparator_1_lt));  // open: gt, eq
  assign slt0 = {{31{1'b0}}, comparator_1_lt};  // Bit_Extender bit_extender_6

  // Notes on the sheet:
  //   INPUTS to your circuit
  //   DON'T CHANGE THE LOCATIONS OF THE INPUTS AND OUTPUTS!
  //   OUTPUT from your circuit
endmodule
