// Logisim project control_logic.circ as structural Verilog: 1 circuit, main circuit control_logic
module control_logic (
  input  [31:0] inst,
  input  BrEq,
  input  BrLt,
  output PCSel,
  output RegWEn,
  output [2:0] ImmSel,
  output BrUn,
  output ASel,
  output BSel,
  output [3:0] ALUSel,
  output MemRW,
  output [1:0] WBSel
);

  wire and_2_out, and_3_out, and_4_out, and_5_out, and_6_out, and_7_out, and_8_out, and_9_out, and_10_out,
       and_11_out, and_12_out, and_13_out, not_1_out, not_2_out, not_3_out, not_4_out, not_5_out, not_6_out,
       not_7_out, not_8_out, not_9_out, not_10_out, not_11_out, not_12_out, not_13_out, not_14_out,
       not_15_out, not_16_out, not_17_out, not_18_out, not_19_out, not_20_out, not_21_out, not_22_out,
       not_23_out, not_24_out, not_25_out, not_26_out, not_27_out, not_28_out, not_29_out, not_30_out,
       not_31_out, not_32_out, not_33_out, not_34_out, not_35_out, sel0, sel1, sel2, sel3;

  not not_1 (not_1_out, inst[3]);
  not not_2 (not_2_out, inst[4]);
  and and_1 (sel3, inst[2], not_1_out, not_2_out, inst[5], inst[6]);
  not not_3 (not_3_out, inst[3]);
  not not_4 (not_4_out, inst[2]);
  not not_5 (not_5_out, inst[3]);
  not not_6 (not_6_out, inst[4]);
  and and_2 (and_2_out, inst[5], not_6_out, not_5_out, not_4_out, inst[6]);
  not not_7 (not_7_out, inst[3]);
  not not_8 (not_8_out, inst[5]);
  not not_9 (not_9_out, inst[6]);
  and and_3 (and_3_out, inst[2], not_7_out, inst[4], not_11_out, inst[5]);
  and and_4 (and_4_out, inst[2], not_3_out, inst[4], not_8_out, not_9_out);
  or or_1 (sel2, and_2_out, and_4_out, and_3_out, and_5_out);
  not not_10 (not_10_out, inst[4]);
  not not_11 (not_11_out, inst[6]);
  and and_5 (and_5_out, inst[2], inst[3], not_10_out, inst[5], inst[6]);
  Multiplexer #(.select(4), .width(2), .enable("false")) multiplexer_1 (
    .in0(2'b01), .out(WBSel), .sel({sel3, sel2, sel1, sel0}));  // open: in1, in2, in3, in4, in5, in6, in7, in8, in9, in10, in11, in12, in13, in14, in15
  not not_12 (not_12_out, inst[2]);
  not not_13 (not_13_out, inst[2]);
  not not_14 (not_14_out, inst[6]);
  not not_15 (not_15_out, inst[5]);
  not not_16 (not_16_out, inst[3]);
  and and_6 (and_6_out, not_16_out, not_15_out, not_14_out, not_13_out, inst[4]);
  not not_17 (not_17_out, inst[6]);
  not not_18 (not_18_out, inst[3]);
  not not_19 (not_19_out, inst[4]);
  and and_7 (and_7_out, not_12_out, not_18_out, not_19_out, inst[5], not_17_out);
  or or_2 (sel1, and_6_out, and_7_out, and_9_out, and_8_out);
  not not_20 (not_20_out, inst[4]);
  not not_21 (not_21_out, inst[6]);
  not not_22 (not_22_out, inst[3]);
  and and_8 (and_8_out, inst[2], inst[3], not_20_out, inst[5], inst[6]);
  and and_9 (and_9_out, inst[2], inst[4], not_22_out, not_21_out, inst[5]);
  not not_23 (not_23_out, inst[5]);
  not not_24 (not_24_out, inst[2]);
  not not_25 (not_25_out, inst[4]);
  not not_26 (not_26_out, inst[3]);
  and and_10 (and_10_out, not_24_out, not_26_out, not_25_out, not_23_out, not_29_out);
  not not_27 (not_27_out, inst[3]);
  not not_28 (not_28_out, inst[2]);
  not not_29 (not_29_out, inst[6]);
  not not_30 (not_30_out, inst[4]);
  and and_11 (and_11_out, not_28_out, not_27_out, not_30_out, inst[5], not_31_out);
  not not_31 (not_31_out, inst[6]);
  not not_32 (not_32_out, inst[3]);
  or or_3 (sel0, and_10_out, and_11_out, and_12_out, and_13_out);
  not not_33 (not_33_out, inst[5]);
  not not_34 (not_34_out, inst[6]);
  and and_12 (and_12_out, inst[2], not_32_out, inst[4], not_33_out, not_34_out);
  not not_35 (not_35_out, inst[4]);
  and and_13 (and_13_out, inst[2], inst[3], not_35_out, inst[5], inst[6]);

  // Other names for the same wires on the sheet: opcode[6:0] = inst[6:0]; op2 = inst[2]; op3 = inst[3]; op4 = inst[4];
  //   op5 = inst[5]; op6 = inst[6]; func3[2:0] = inst[14:12]; func7[6:0] = inst[31:25];
  //   typesel[3:0] = {sel3, sel2, sel1, sel0}

  // Notes on the sheet:
  //   INPUTS to your circuit
  //   WBSel
  //   DON'T CHANGE THE LOCATIONS OF THE INPUTS AND OUTPUTS!
  //   OUTPUT from your circuit
  //   TypeSelector
endmodule
