// Logisim project cpu.circ as structural Verilog: 1 circuit, main circuit main
module main (
  input  [31:0] INSTRUCTION,
  input  CLOCK,
  output [31:0] PROGRAM_COUNTER,
  output [31:0] ra,
  output [31:0] sp,
  output [31:0] t0,
  output [31:0] t1,
  output [31:0] t2,
  output [31:0] s0,
  output [31:0] s1,
  output [31:0] a0
);

  wire ASel, branch_comp_1_breq, branch_comp_1_brlt, BSel, control_logic_1_brun, control_logic_1_memrw,
       PCSel, RWen;
  wire [1:0] control_logic_1_wbsel;
  wire [2:0] control_logic_1_immsel;
  wire [3:0] ALUSel;
  wire [31:0] adder_1_out, adder_2_out, ALUr, DMEM_p5, ID_q, imm, multiplexer_1_out, multiplexer_2_out,
       multiplexer_3_out, RegFile_read_data_2, register_1_q, rs1d, WB;

  Multiplexer #(.width(32), .enable("false")) multiplexer_1 (
    .in0(ALUr), .in1(adder_1_out), .out(multiplexer_1_out), .sel(PCSel));
  Adder #(.width(32)) adder_1 (.a(PROGRAM_COUNTER), .b(32'h4), .out(adder_1_out));  // open: cin, cout
  Register #(.width(32)) PC (.D(multiplexer_1_out), .en(1'b1), .clk(CLOCK), .Q(PROGRAM_COUNTER));  // open: clr
  Register #(.width(32)) register_1 (.D(PROGRAM_COUNTER), .en(1'b1), .clk(CLOCK), .Q(register_1_q));  // open: clr
  Register #(.width(32)) ID (.D(INSTRUCTION), .en(1'b1), .clk(CLOCK), .Q(ID_q));  // open: clr
  control_logic control_logic_1 (
    .BSel(BSel), .BrUn(control_logic_1_brun), .RegWEn(RWen), .ImmSel(control_logic_1_immsel), .ASel(ASel),
    .PCSel(PCSel), .BrLt(branch_comp_1_brlt), .BrEq(branch_comp_1_breq), .inst(ID_q), .ALUSel(ALUSel),
    .MemRW(control_logic_1_memrw), .WBSel(control_logic_1_wbsel));
  regfile_main RegFile (
    .rs2(ID_q[19:15]), .rd(ID_q[11:7]), .Read_Data_1(rs1d), .Read_Data_2(RegFile_read_data_2), .ra(ra),
    .sp(sp), .t0(t0), .t1(t1), .t2(t2), .s0(s0), .s1(s1), .a0(a0), .rs1(ID_q[24:20]), .Write_Data(WB),
    .RegWEn(RWen), .clk(CLOCK));
  imm_gen imm_gen_1 (.ImmSel(control_logic_1_immsel), .imm(imm), .inst(ID_q));
  Multiplexer #(.width(32), .enable("false")) multiplexer_2 (
    .in0(register_1_q), .in1(rs1d), .out(multiplexer_2_out), .sel(ASel));
  Multiplexer #(.width(32), .enable("false")) multiplexer_3 (
    .in0(RegFile_read_data_2), .in1(imm), .out(multiplexer_3_out), .sel(BSel));
  alu Arithmetic_Logic_Unit (.ALUSel(ALUSel), .Result(ALUr), .A(multiplexer_2_out), .B(multiplexer_3_out));
  branch_comp branch_comp_1 (
    .BrEq(branch_comp_1_breq), .BrUn(control_logic_1_brun), .rs1(multiplexer_2_out),
    .BrLt(branch_comp_1_brlt), .rs2(multiplexer_3_out));
  // mem_main DMEM: pin names not known; wires that end beside it: ALUr, rs1d, CLOCK, control_logic_1_memrw, DMEM_p5
  Adder #(.width(32)) adder_2 (.a(register_1_q), .b(32'h4), .out(adder_2_out));  // open: cin, cout
  Multiplexer #(.select(2), .width(32), .enable("false")) multiplexer_4 (
    .in0(adder_2_out), .in1(ALUr), .in2(DMEM_p5), .out(WB), .sel(control_logic_1_wbsel));  // open: in3

  // Other names for the same wires on the sheet: clk = CLOCK

  // Notes on the sheet:
  //   Output
  //   IMEM (do **NOT** move this)
  //   Inputs
  //   It is OK to move the PC, RegFile, ALU, MEM, Branch Comp, Imm Gen, and Control Logic to wherever is most convenient for you when constructing your CPU, and to delete this text
  //   Inputs/Outputs for testing. Do **NOT** move these.
endmodule
